# Fritzing sketch Arudino Workshop Day 1 Schematic (saved by Fritzing 0.9.3b)
breadboards: 1

parts:
  Part1 = Arduino Uno (Rev3)
  LED1 = LED - 5mm [color="Red (633nm)" package="5 mm [THT]"]
  S1 = Pushbutton [package="[THT]"]
  R1 = Resistor [tolerance=±5% resistance=220 package=THT]

nets:
  N1: Part1.D13/SCK, LED1.anode
  N2: Part1.D2, S1.Pin_3, S1.Pin_4, R1.Pin_0
  N3: Part1.5V, R1.Pin_1
  N4: Part1.GND, LED1.cathode, S1.Pin_1, S1.Pin_2
